# Fritzing sketch RobotBasico (saved by Fritzing 0.9.3b)
breadboards: 1

parts:
  S1 = H-Bridge with L298N
  BT1 = Bluetooth HC-06u [package=THT]
  Componente1 = Arduino Mega 2560 (Rev3)
  M1 = DC Motor
  M2 = DC Motor
  VCC1 = Battery block 9V

nets:
  N1: S1.12V, VCC1.+
  GND: S1.GND, BT1.GND, Componente1.GND, VCC1.-
  N2: S1.IN1, Componente1.D2_PWM
  N3: S1.IN2, Componente1.D3_PWM
  N4: S1.IN3, Componente1.D4_PWM
  N5: S1.IN4, Componente1.D5_PWM
  N6: S1.M1-01, M2.pin_2
  N7: S1.M1-02, M2.pin_1
  N8: S1.M2-01, M1.pin_2
  N9: S1.M2-02, M1.pin_1
  VCC: BT1.VCC, Componente1.5V
  N10: BT1.TXD, Componente1.D19/RX1
  N11: BT1.RXD, Componente1.D18/TX1

custom parts:
  H-Bridge with L298N: h-bridge
  Bluetooth HC-06u: Bluetooth HC-06 - face up, pins down 16.5mm x 37.5mm PCB
